// Logisim project Project2.circ as structural Verilog: 9 circuits, main circuit MIPS32
module MIPS32 (
  input  in_1,
  input  in_2
);

  wire clock_1_out, ctrlidex_1_com, ctrlidex_1_imm, ctrlidex_1_su, registerfile_1_p3;
  wire [3:0] ctrlidex_1_alu;
  wire [4:0] decode_1_ra, decode_1_rb, registerfile_1_p4;
  wire [31:0] bit_extender_1_out, compare_1_o, CTRL_2_q, CTRL_q, ctrlidex_1_ctrl, D_q, idex_1_qa, idex_1_qb,
       idex_1_qimm, incrementer4_1_out_2, mips_alu_1_p4, mips_alu_1_p5, mipsprogramrom_1_p2,
       multiplexer_1_out, pc_1_o, register_1_q, registerfile_1_p1, registerfile_1_p7, registerfile_1_p8;

  PC pc_1 (.I(incrementer4_1_out_2), .Reset(in_1), .C(clock_1_out), .Reset2(in_2), .O(pc_1_o));
  Incrementer4 incrementer4_1 (.in_1(pc_1_o), .out_2(incrementer4_1_out_2));
  // Probe on incrementer4_1_out_2
  // MIPSProgramROM mipsprogramrom_1: pin names not known; wires that end beside it: pc_1_o, mipsprogramrom_1_p2
  Register #(.width(32)) register_1 (.D(mipsprogramrom_1_p2), .clk(clock_1_out), .Q(register_1_q));  // open: en, clr
  Clock clock_1 (.out(clock_1_out));
  decode decode_1 (.I(register_1_q), .rB(decode_1_rb), .rA(decode_1_ra));
  // RegisterFile registerfile_1: pin names not known; wires that end beside it: registerfile_1_p1, clock_1_out, registerfile_1_p3, registerfile_1_p4, decode_1_ra, decode_1_rb, registerfile_1_p7, registerfile_1_p8, register_1_q[15:0]
  RWD rwd_1 (.Ctrl(CTRL_2_q), .dest(registerfile_1_p4), .WE(registerfile_1_p3));
  Bit_Extender #(.in_width(16), .out_width(32)) bit_extender_1 (.out(bit_extender_1_out));  // open: in
  IDEX idex_1 (
    .C(clock_1_out), .DA(registerfile_1_p7), .DB(registerfile_1_p8), .DIMM(bit_extender_1_out),
    .QA(idex_1_qa), .QB(idex_1_qb), .QIMM(idex_1_qimm));
  CtrlIDEX ctrlidex_1 (
    .D(register_1_q), .C(clock_1_out), .IMM(ctrlidex_1_imm), .Ctrl(ctrlidex_1_ctrl), .Com(ctrlidex_1_com),
    .SU(ctrlidex_1_su), .ALU(ctrlidex_1_alu));
  Multiplexer #(.width(32), .enable("false")) multiplexer_1 (
    .in0(idex_1_qb), .in1(idex_1_qimm), .out(multiplexer_1_out), .sel(ctrlidex_1_imm));
  // Mips_ALU mips_alu_1: pin names not known; wires that end beside it: idex_1_qa, multiplexer_1_out, ctrlidex_1_alu, mips_alu_1_p4, mips_alu_1_p5
  compare compare_1 (.A(idex_1_qa), .B(multiplexer_1_out), .SU(ctrlidex_1_su), .O(compare_1_o));
  Multiplexer #(.width(32), .enable("false")) multiplexer_2 (
    .in0(mips_alu_1_p4), .in1(compare_1_o), .out(mips_alu_1_p5), .sel(ctrlidex_1_com));
  Register #(.width(32)) D (.D(mips_alu_1_p5), .clk(clock_1_out), .Q(D_q));  // open: en, clr
  Register #(.width(32)) CTRL (.D(ctrlidex_1_ctrl), .clk(clock_1_out), .Q(CTRL_q));  // open: en, clr
  Register #(.width(32)) D_2 (.D(D_q), .clk(clock_1_out), .Q(registerfile_1_p1));  // open: en, clr
  Register #(.width(32)) CTRL_2 (.D(CTRL_q), .clk(clock_1_out), .Q(CTRL_2_q));  // open: en, clr
endmodule

module Incrementer4 (
  input  [31:0] in_1,
  output [31:0] out_2
);

  wire bit_extender_1_out, incrementer_1_p2, not_1_out;
  wire [1:1] and_1_out;
  wire [29:0] bit_extender_2_out;

  Bit_Extender #(.in_width(32), .out_width(1), .\type ("zero")) bit_extender_1 (.in(in_1), .out(bit_extender_1_out));
  and and_1 (and_1_out[1], bit_extender_1_out, not_1_out);
  not not_1 (not_1_out, bit_extender_1_out);
  // Incrementer #(.width(1)) incrementer_1: pin names not known; wires that end beside it: and_1_out[1], incrementer_1_p2
  assign bit_extender_2_out = {{29{1'b0}}, incrementer_1_p2};  // Bit_Extender bit_extender_2
  assign out_2 = {bit_extender_2_out, {2{and_1_out[1]}}} ^ in_1;  // XOR_Gate xor_1, 32 bits wide
endmodule

module PC (
  input  [31:0] I,
  input  Reset,
  input  C,
  input  Reset2,
  output [31:0] O
);

  wire not_1_out, or_1_out;
  wire [31:0] multiplexer_1_out;

  Multiplexer #(.width(32), .enable("false")) multiplexer_1 (
    .in0({32{1'b0}}), .in1(I), .out(multiplexer_1_out), .sel(not_1_out));
  not not_1 (not_1_out, Reset);
  or or_1 (or_1_out, C, Reset2);
  Register #(.width(32)) register_1 (.D(multiplexer_1_out), .clk(or_1_out), .Q(O));  // open: en, clr
endmodule

module IDEX (
  input  C,
  input  [31:0] DA,
  input  [31:0] DB,
  input  [31:0] DIMM,
  output [31:0] QA,
  output [31:0] QB,
  output [31:0] QIMM
);

  Register #(.width(32)) register_1 (.D(DA), .clk(C), .Q(QA));  // open: en, clr
  Register #(.width(32)) register_2 (.D(DB), .clk(C), .Q(QB));  // open: en, clr
  Register #(.width(32)) register_3 (.D(DIMM), .clk(C), .Q(QIMM));  // open: en, clr
endmodule

module CtrlIDEX (
  input  [31:0] D,
  input  C,
  output IMM,
  output [31:0] Ctrl,
  output Com,
  output SU,
  output [3:0] ALU
);

  wire and_1_out, and_2_out, and_3_out, and_4_out, and_5_out, and_6_out, and_7_out, and_8_out, and_9_out,
       and_10_out, and_11_out, and_12_out, not_1_out, not_2_out, not_3_out, not_4_out, not_5_out, not_6_out,
       not_7_out, not_8_out, not_9_out, not_10_out, not_11_out, not_12_out, not_13_out, not_14_out,
       not_15_out, not_16_out, not_17_out, not_18_out;

  Register #(.width(32)) register_1 (.D(D), .clk(C), .Q(Ctrl));  // open: en, clr
  not not_1 (not_1_out, Ctrl[27]);
  not not_2 (not_2_out, Ctrl[29]);
  and and_1 (and_1_out, Ctrl[31], Ctrl[26]);
  not not_3 (not_3_out, Ctrl[31]);
  not not_4 (not_4_out, Ctrl[29]);
  not not_5 (not_5_out, Ctrl[31]);
  not not_6 (not_6_out, Ctrl[30]);
  not not_7 (not_7_out, Ctrl[28]);
  not not_8 (not_8_out, Ctrl[31]);
  not not_9 (not_9_out, Ctrl[30]);
  not not_10 (not_10_out, Ctrl[28]);
  not not_11 (not_11_out, Ctrl[31]);
  not not_12 (not_12_out, Ctrl[30]);
  not not_13 (not_13_out, Ctrl[27]);
  not not_14 (not_14_out, Ctrl[31]);
  not not_15 (not_15_out, Ctrl[30]);
  not not_16 (not_16_out, Ctrl[26]);
  not not_17 (not_17_out, Ctrl[30]);
  not not_18 (not_18_out, Ctrl[28]);
  and and_2 (and_2_out, Ctrl[29], not_1_out);
  and and_3 (and_3_out, Ctrl[29], Ctrl[28]);
  and and_4 (and_4_out, Ctrl[31], Ctrl[28]);
  and and_5 (and_5_out, not_2_out, Ctrl[27]);
  and and_6 (and_6_out, Ctrl[29], Ctrl[28]);
  or or_1 (ALU[1], Ctrl[29], and_1_out);
  and and_7 (and_7_out, not_3_out, not_4_out, Ctrl[26]);
  and and_8 (and_8_out, Ctrl[29], Ctrl[28]);
  and and_9 (and_9_out, not_5_out, not_6_out, Ctrl[29], not_7_out, Ctrl[26]);
  and and_10 (and_10_out, not_8_out, not_9_out, Ctrl[29], not_10_out, Ctrl[27]);
  and and_11 (and_11_out, not_11_out, not_12_out, Ctrl[29], Ctrl[28], not_13_out);
  and and_12 (and_12_out, not_14_out, not_15_out, Ctrl[29], Ctrl[28], not_16_out);
  and and_13 (Com, not_17_out, Ctrl[29], not_18_out, Ctrl[27]);
  and and_14 (SU, ~Ctrl[30], Ctrl[29], ~Ctrl[28], Ctrl[27], Ctrl[26]);  // AND_Gate
  or or_2 (ALU[3], and_2_out, and_3_out, and_4_out);
  or or_3 (ALU[2], and_5_out, and_6_out);
  or or_4 (ALU[0], and_7_out, and_8_out);
  or or_5 (IMM, and_9_out, and_10_out, and_11_out, and_12_out);
endmodule

module RWD (
  input  [31:0] Ctrl,
  output [4:0] dest,
  output WE
);

  wire and_1_out, and_2_out, and_3_out, and_4_out, and_5_out, and_6_out, and_7_out, and_8_out, and_9_out,
       not_1_out, not_2_out, not_3_out, not_4_out, not_5_out, not_6_out, not_7_out, not_8_out, not_9_out,
       not_10_out, not_11_out, not_12_out, not_13_out, not_14_out, not_15_out, not_16_out, not_17_out,
       not_18_out, not_19_out, not_20_out, not_21_out, not_22_out, not_23_out, not_24_out, not_25_out,
       not_26_out, not_27_out, or_1_out, or_2_out;

  not not_1 (not_1_out, Ctrl[5]);
  not not_2 (not_2_out, Ctrl[4]);
  not not_3 (not_3_out, Ctrl[3]);
  not not_4 (not_4_out, Ctrl[0]);
  not not_5 (not_5_out, Ctrl[5]);
  not not_6 (not_6_out, Ctrl[4]);
  not not_7 (not_7_out, Ctrl[3]);
  not not_8 (not_8_out, Ctrl[5]);
  not not_9 (not_9_out, Ctrl[4]);
  not not_10 (not_10_out, Ctrl[2]);
  not not_11 (not_11_out, Ctrl[4]);
  not not_12 (not_12_out, Ctrl[3]);
  not not_13 (not_13_out, Ctrl[0]);
  not not_14 (not_14_out, Ctrl[4]);
  not not_15 (not_15_out, Ctrl[3]);
  not not_16 (not_16_out, Ctrl[31]);
  not not_17 (not_17_out, Ctrl[30]);
  not not_18 (not_18_out, Ctrl[28]);
  not not_19 (not_19_out, Ctrl[31]);
  not not_20 (not_20_out, Ctrl[30]);
  not not_21 (not_21_out, Ctrl[28]);
  not not_22 (not_22_out, Ctrl[31]);
  not not_23 (not_23_out, Ctrl[30]);
  not not_24 (not_24_out, Ctrl[27]);
  not not_25 (not_25_out, Ctrl[31]);
  not not_26 (not_26_out, Ctrl[30]);
  not not_27 (not_27_out, Ctrl[26]);
  and and_1 (and_1_out, not_1_out, not_2_out, not_3_out, not_4_out);
  and and_2 (and_2_out, not_5_out, not_6_out, not_7_out, Ctrl[1]);
  and and_3 (and_3_out, not_8_out, not_9_out, not_10_out, Ctrl[1]);
  and and_4 (and_4_out, not_11_out, not_12_out, Ctrl[2], not_13_out);
  and and_5 (and_5_out, Ctrl[5], not_14_out, not_15_out, Ctrl[0]);
  and and_6 (and_6_out, not_16_out, not_17_out, Ctrl[29], not_18_out, Ctrl[26]);
  and and_7 (and_7_out, not_19_out, not_20_out, Ctrl[29], not_21_out, Ctrl[27]);
  and and_8 (and_8_out, not_22_out, not_23_out, Ctrl[29], Ctrl[28], not_24_out);
  and and_9 (and_9_out, not_25_out, not_26_out, Ctrl[29], Ctrl[28], not_27_out);
  or or_1 (or_1_out, and_1_out, and_2_out, and_3_out, and_4_out, and_5_out);
  Multiplexer #(.width(5), .enable("false")) multiplexer_1 (
    .in0(Ctrl[15:11]), .in1(Ctrl[20:16]), .out(dest), .sel(or_2_out));
  or or_2 (or_2_out, and_6_out, and_7_out, and_8_out, and_9_out);
  or or_3 (WE, or_2_out, or_1_out);

  // Notes on the sheet:
  //   dest.
endmodule

module compare (
  input  [31:0] A,
  input  [31:0] B,
  input  SU,
  output [31:0] O
);

  wire comparator_1_eq, comparator_2_eq, multiplexer_1_out;

  Comparator #(.width(32)) comparator_1 (.a(A), .b(B), .eq(comparator_1_eq));  // open: gt, lt
  Comparator #(.width(32), .mode("unsigned")) comparator_2 (.a(A), .b(B), .eq(comparator_2_eq));  // open: gt, lt
  Multiplexer #(.enable("false")) multiplexer_1 (
    .in0(comparator_1_eq), .in1(comparator_2_eq), .out(multiplexer_1_out), .sel(SU));
  assign O = {{31{1'b0}}, multiplexer_1_out};  // Bit_Extender bit_extender_1

  // Notes on the sheet:
  //   signed
  //   unsigned
endmodule

module decode (
  input  [31:0] I,
  output [4:0] rB,
  output [4:0] rA
);


  assign rA = I[25:21];
  assign rB = I[20:16];
endmodule

module test (
  input  I5,
  input  I4,
  input  I3,
  input  I2,
  input  I1,
  input  I0,
  output O
);

  wire and_1_out, and_2_out, and_3_out, and_4_out, and_5_out, not_1_out, not_2_out, not_3_out, not_4_out,
       not_5_out, not_6_out, not_7_out, not_8_out, not_9_out, not_10_out, not_11_out, not_12_out, not_13_out,
       not_14_out, not_15_out;

  not not_1 (not_1_out, I5);
  not not_2 (not_2_out, I4);
  not not_3 (not_3_out, I3);
  not not_4 (not_4_out, I0);
  not not_5 (not_5_out, I5);
  not not_6 (not_6_out, I4);
  not not_7 (not_7_out, I3);
  not not_8 (not_8_out, I5);
  not not_9 (not_9_out, I4);
  not not_10 (not_10_out, I2);
  not not_11 (not_11_out, I4);
  not not_12 (not_12_out, I3);
  not not_13 (not_13_out, I0);
  not not_14 (not_14_out, I4);
  not not_15 (not_15_out, I3);
  and and_1 (and_1_out, not_1_out, not_2_out, not_3_out, not_4_out);
  and and_2 (and_2_out, not_5_out, not_6_out, not_7_out, I1);
  and and_3 (and_3_out, not_8_out, not_9_out, not_10_out, I1);
  and and_4 (and_4_out, not_11_out, not_12_out, I2, not_13_out);
  and and_5 (and_5_out, I5, not_14_out, not_15_out, I0);
  or or_1 (O, and_1_out, and_2_out, and_3_out, and_4_out, and_5_out);
endmodule
